# Fritzing sketch Untitled Sketch 3 (saved by Fritzing 0.9.3b)
breadboards: 1

parts:
  LED1 = LED - 5mm [color="Red (633nm)" package="5 mm [THT]"]
  R1 = Resistor [tolerance=±5% resistance=470k package="0805 [SMD]"]
  Part1 = Arduino Uno (Rev3) - ICSP

nets:
  N1: LED1.cathode, R1.Pin_1
  N2: LED1.anode, Part1.D9_PWM
  N3: R1.Pin_0, Part1.GND
